// Logisim project cpu_32 _single_cycle.circ as structural Verilog: 6 circuits, main circuit main
module main (
);

  wire clock_1_out, control_unit_1_alu_b_operand_select, control_unit_1_alu_cmp_type,
       control_unit_1_pc_select, control_unit_1_reg_write, undriven;
  wire [1:0] control_unit_1_ram_write_type;
  wire [2:0] alu_1_eq, control_unit_1_imm_type_select, control_unit_1_ram_read_type,
       control_unit_1_write_data_select;
  wire [3:0] control_unit_1_alu_op_type;
  wire [31:0] adder_1_out, adder_2_out, alu_1_alu_result, bit_extender_1_out, DATA_MEMORY_ram_out,
       imm_select_1_imm, INSTR_MEMORY_ram_out, multiplexer_1_out, multiplexer_2_out, multiplexer_3_out, PC_q,
       reg_file_1_read_1, reg_file_1_read_2;

  Clock clock_1 (.out(clock_1_out));
  Adder #(.width(32)) adder_1 (.a(PC_q), .b(32'h4), .out(adder_1_out));  // open: cin, cout
  Multiplexer #(.width(32)) multiplexer_1 (
    .in0(adder_1_out), .in1(adder_2_out), .out(multiplexer_1_out), .sel(control_unit_1_pc_select));
  Register #(.width(32)) PC (.D(multiplexer_1_out), .en(1'b1), .clk(clock_1_out), .Q(PC_q), .clr(undriven));
  byte_adrr_ram INSTR_MEMORY (
    .READ_CTRL(3'b000), .WRITE_CTRL(2'b11), .WORD_ADDR(PC_q), .CLK(clock_1_out),
    .RAM_OUT(INSTR_MEMORY_ram_out));  // open: DATA_IN
  control_unit control_unit_1 (
    .INSTR(INSTR_MEMORY_ram_out), .ALU_FLAGS({{2{alu_1_eq[2]}}, alu_1_eq[0]}),
    .WRITE_DATA_SELECT(control_unit_1_write_data_select), .RAM_WRITE_TYPE(control_unit_1_ram_write_type),
    .RAM_READ_TYPE(control_unit_1_ram_read_type), .ALU_OP_TYPE(control_unit_1_alu_op_type),
    .ALU_CMP_TYPE(control_unit_1_alu_cmp_type), .ALU_B_OPERAND_SELECT(control_unit_1_alu_b_operand_select),
    .REG_WRITE(control_unit_1_reg_write), .IMM_TYPE_SELECT(control_unit_1_imm_type_select),
    .PC_SELECT(control_unit_1_pc_select));
  imm_select imm_select_1 (
    .INSTR(INSTR_MEMORY_ram_out), .control(control_unit_1_imm_type_select), .IMM(imm_select_1_imm));
  Adder #(.width(32)) adder_2 (.a(imm_select_1_imm), .b(PC_q), .out(adder_2_out));  // open: cin, cout
  reg_file reg_file_1 (
    .ADR_2(INSTR_MEMORY_ram_out[24:20]), .CLK(clock_1_out), .WRITE_ENABLE(control_unit_1_reg_write),
    .WRITE_ADR(INSTR_MEMORY_ram_out[11:7]), .DATA_IN(multiplexer_3_out), .ADR_1(INSTR_MEMORY_ram_out[19:15]),
    .READ_2(reg_file_1_read_2), .READ_1(reg_file_1_read_1));
  Multiplexer #(.width(32)) multiplexer_2 (
    .in0(reg_file_1_read_2), .in1(imm_select_1_imm), .out(multiplexer_2_out),
    .sel(control_unit_1_alu_b_operand_select));
  alu alu_1 (
    .in_2(reg_file_1_read_1), .in_3(multiplexer_2_out), .ALU_CMPR_CTRL(control_unit_1_alu_cmp_type),
    .ALU_OP_CTRL(control_unit_1_alu_op_type), .LT(alu_1_eq[2]), .GT(alu_1_eq[2]), .EQ(alu_1_eq[0]),
    .ALU_RESULT(alu_1_alu_result));
  assign bit_extender_1_out = {{31{alu_1_eq[2]}}, alu_1_eq[2]};  // Bit_Extender bit_extender_1
  byte_adrr_ram DATA_MEMORY (
    .READ_CTRL(control_unit_1_ram_read_type), .DATA_IN(reg_file_1_read_2),
    .WRITE_CTRL(control_unit_1_ram_write_type), .WORD_ADDR(alu_1_alu_result), .CLK(clock_1_out),
    .RAM_OUT(DATA_MEMORY_ram_out));
  Multiplexer #(.select(3), .width(32)) multiplexer_3 (
    .in2(bit_extender_1_out), .in3(alu_1_alu_result), .in4(imm_select_1_imm), .in5(DATA_MEMORY_ram_out),
    .in6(adder_1_out), .in7(adder_2_out), .out(multiplexer_3_out), .sel(control_unit_1_write_data_select));  // open: in0, in1

  // Notes on the sheet:
  //   F3_32SC :)
  //   PC
  //   RD
  //   RS1
  //   RS2
  //   PC+IM
  //   ALU_RESULT
  //   LT
  //   IM
  //   PC+4
endmodule

module alu (
  input  [3:0] ALU_OP_CTRL,
  input  [31:0] in_2,
  input  [31:0] in_3,
  input  ALU_CMPR_CTRL,
  output [31:0] ALU_RESULT,
  output GT,
  output EQ,
  output LT
);

  wire comparator_1_eq, comparator_1_gt, comparator_1_lt, comparator_2_eq, comparator_2_gt, comparator_2_lt;
  wire [4:0] bit_extender_1_out, bit_extender_2_out, bit_extender_3_out;
  wire [31:0] adder_1_out, and_1_out, divider_1_out, divider_1_rem, divider_2_out, divider_2_rem,
       multiplier_1_cout, multiplier_1_out, or_1_out, shifter_1_out, shifter_2_out, shifter_3_out,
       subtractor_1_out, xor_1_out;

  assign or_1_out = in_3 | in_2;  // OR_Gate or_1, 32 bits wide
  assign xor_1_out = in_3 ^ in_2;  // XOR_Gate xor_1, 32 bits wide
  assign and_1_out = in_3 & in_2;  // AND_Gate and_1, 32 bits wide
  Adder #(.width(32)) adder_1 (.a(in_2), .b(in_3), .out(adder_1_out));  // open: cin, cout
  Shifter #(.width(32)) shifter_1 (.in(in_2), .\dist (bit_extender_1_out), .out(shifter_1_out));
  Bit_Extender #(.in_width(32), .out_width(5)) bit_extender_1 (.in(in_3), .out(bit_extender_1_out));
  Shifter #(.shift("lr"), .width(32)) shifter_2 (.in(in_2), .\dist (bit_extender_2_out), .out(shifter_2_out));
  Bit_Extender #(.in_width(32), .out_width(5)) bit_extender_2 (.in(in_3), .out(bit_extender_2_out));
  Shifter #(.shift("ar"), .width(32)) shifter_3 (.in(in_2), .\dist (bit_extender_3_out), .out(shifter_3_out));
  Bit_Extender #(.in_width(32), .out_width(5)) bit_extender_3 (.in(in_3), .out(bit_extender_3_out));
  Subtractor #(.width(32)) subtractor_1 (.a(in_2), .b(in_3), .out(subtractor_1_out));  // open: bin, bout
  Comparator #(.width(32)) comparator_1 (
    .a(in_2), .b(in_3), .gt(comparator_1_gt), .eq(comparator_1_eq), .lt(comparator_1_lt));
  Comparator #(.mode("unsigned"), .width(32)) comparator_2 (
    .a(in_2), .b(in_3), .gt(comparator_2_gt), .eq(comparator_2_eq), .lt(comparator_2_lt));
  Multiplexer multiplexer_1 (.in0(comparator_1_gt), .in1(comparator_2_gt), .out(GT), .sel(ALU_CMPR_CTRL));
  Multiplexer multiplexer_2 (.in0(comparator_1_eq), .in1(comparator_2_eq), .out(EQ), .sel(ALU_CMPR_CTRL));
  Multiplexer multiplexer_3 (.in0(comparator_1_lt), .in1(comparator_2_lt), .out(LT), .sel(ALU_CMPR_CTRL));
  Multiplier #(.mode("twosComplement"), .width(32)) multiplier_1 (
    .a(in_3), .b(in_2), .out(multiplier_1_out), .cout(multiplier_1_cout));  // open: cin
  Divider #(.width(32)) divider_1 (
    .a(in_3), .b(in_2), .out(divider_1_out), .upper(multiplier_1_cout), .rem(divider_1_rem));
  Divider #(.mode("twosComplement"), .width(32)) divider_2 (
    .a(in_3), .b(in_2), .out(divider_2_out), .rem(divider_2_rem));  // open: upper
  Multiplexer #(.select(4), .width(32)) multiplexer_4 (
    .in0(xor_1_out), .in1(and_1_out), .in2(adder_1_out), .in3(shifter_1_out), .in4(shifter_2_out),
    .in5(shifter_3_out), .in6(subtractor_1_out), .in7(or_1_out), .in8(multiplier_1_out), .in9(divider_2_out),
    .in10(divider_1_out), .in11(divider_2_rem), .in12(divider_1_rem), .out(ALU_RESULT), .sel(ALU_OP_CTRL));  // open: in13, in14, in15

  // Notes on the sheet:
  //   A+B
  //   A-B
endmodule

module reg_file (
  input  [4:0] ADR_2,
  input  [4:0] ADR_1,
  input  WRITE_ENABLE,
  input  [4:0] WRITE_ADR,
  input  [31:0] DATA_IN,
  input  CLK,
  output [31:0] READ_1,
  output [31:0] READ_2
);

  wire decoder_1_out1, decoder_1_out2, decoder_1_out3, decoder_1_out4, decoder_1_out5, decoder_1_out6,
       decoder_1_out7, decoder_1_out8, decoder_1_out9, decoder_1_out10, decoder_1_out11, decoder_1_out12,
       decoder_1_out13, decoder_1_out14, decoder_1_out15, decoder_1_out16, decoder_1_out17, decoder_1_out18,
       decoder_1_out19, decoder_1_out20, decoder_1_out21, decoder_1_out22, decoder_1_out23, decoder_1_out24,
       decoder_1_out25, decoder_1_out26, decoder_1_out27, decoder_1_out28, decoder_1_out29, decoder_1_out30,
       decoder_1_out31;
  wire [31:0] undriven, undriven_2, x1_q, x2_q, x3_q, x4_q, x5_q, x6_q, x7_q, x8_q, x9_q, x10_q, x11_q,
       x12_q, x13_q, x14_q, x15_q, x16_q, x17_q, x19_q, x20_q, x21_q, x23_q, x24_q, x25_q, x26_q, x27_q,
       x28_q, x29_q, x30_q, x31_q;

  Decoder #(.select(5)) decoder_1 (
    .out1(decoder_1_out1), .out2(decoder_1_out2), .out3(decoder_1_out3), .out4(decoder_1_out4),
    .out5(decoder_1_out5), .out6(decoder_1_out6), .out7(decoder_1_out7), .out8(decoder_1_out8),
    .out9(decoder_1_out9), .out10(decoder_1_out10), .out11(decoder_1_out11), .out12(decoder_1_out12),
    .out13(decoder_1_out13), .out14(decoder_1_out14), .out15(decoder_1_out15), .out16(decoder_1_out16),
    .out17(decoder_1_out17), .out18(decoder_1_out18), .out19(decoder_1_out19), .out20(decoder_1_out20),
    .out21(decoder_1_out21), .out22(decoder_1_out22), .out23(decoder_1_out23), .out24(decoder_1_out24),
    .out25(decoder_1_out25), .out26(decoder_1_out26), .out27(decoder_1_out27), .out28(decoder_1_out28),
    .out29(decoder_1_out29), .out30(decoder_1_out30), .out31(decoder_1_out31), .sel(WRITE_ADR),
    .en(WRITE_ENABLE));  // open: out0
  Register #(.width(32)) x1 (.D(DATA_IN), .en(decoder_1_out1), .clk(CLK), .Q(x1_q));  // open: clr
  Register #(.width(32)) x2 (.D(DATA_IN), .en(decoder_1_out2), .clk(CLK), .Q(x2_q));  // open: clr
  Register #(.width(32)) x3 (.D(DATA_IN), .en(decoder_1_out3), .clk(CLK), .Q(x3_q));  // open: clr
  Register #(.width(32)) x4 (.D(DATA_IN), .en(decoder_1_out4), .clk(CLK), .Q(x4_q));  // open: clr
  Register #(.width(32)) x5 (.D(DATA_IN), .en(decoder_1_out5), .clk(CLK), .Q(x5_q));  // open: clr
  Register #(.width(32)) x6 (.D(DATA_IN), .en(decoder_1_out6), .clk(CLK), .Q(x6_q));  // open: clr
  Register #(.width(32)) x7 (.D(DATA_IN), .en(decoder_1_out7), .clk(CLK), .Q(x7_q));  // open: clr
  Register #(.width(32)) x8 (.D(DATA_IN), .en(decoder_1_out8), .clk(CLK), .Q(x8_q));  // open: clr
  Register #(.width(32)) x9 (.D(DATA_IN), .en(decoder_1_out9), .clk(CLK), .Q(x9_q));  // open: clr
  Register #(.width(32)) x10 (.D(DATA_IN), .en(decoder_1_out10), .clk(CLK), .Q(x10_q));  // open: clr
  Register #(.width(32)) x11 (.D(DATA_IN), .en(decoder_1_out11), .clk(CLK), .Q(x11_q));  // open: clr
  Register #(.width(32)) x12 (.D(DATA_IN), .en(decoder_1_out12), .clk(CLK), .Q(x12_q));  // open: clr
  Register #(.width(32)) x13 (.D(DATA_IN), .en(decoder_1_out13), .clk(CLK), .Q(x13_q));  // open: clr
  Register #(.width(32)) x14 (.D(DATA_IN), .en(decoder_1_out14), .clk(CLK), .Q(x14_q));  // open: clr
  Register #(.width(32)) x15 (.D(DATA_IN), .en(decoder_1_out15), .clk(CLK), .Q(x15_q));  // open: clr
  Register #(.width(32)) x16 (.D(DATA_IN), .en(decoder_1_out16), .clk(CLK), .Q(x16_q));  // open: clr
  Register #(.width(32)) x17 (.D(DATA_IN), .en(decoder_1_out17), .clk(CLK), .Q(x17_q));  // open: clr
  Register #(.width(32)) x18 (.D(DATA_IN), .en(decoder_1_out18), .clk(CLK));  // open: Q, clr
  Register #(.width(32)) x19 (.D(DATA_IN), .en(decoder_1_out19), .clk(CLK), .Q(x19_q));  // open: clr
  Register #(.width(32)) x20 (.D(DATA_IN), .en(decoder_1_out20), .clk(CLK), .Q(x20_q));  // open: clr
  Register #(.width(32)) x21 (.D(DATA_IN), .en(decoder_1_out21), .clk(CLK), .Q(x21_q));  // open: clr
  Register #(.width(32)) x22 (.D(DATA_IN), .en(decoder_1_out22), .clk(CLK));  // open: Q, clr
  Register #(.width(32)) x23 (.D(DATA_IN), .en(decoder_1_out23), .clk(CLK), .Q(x23_q));  // open: clr
  Register #(.width(32)) x24 (.D(DATA_IN), .en(decoder_1_out24), .clk(CLK), .Q(x24_q));  // open: clr
  Register #(.width(32)) x25 (.D(DATA_IN), .en(decoder_1_out25), .clk(CLK), .Q(x25_q));  // open: clr
  Register #(.width(32)) x26 (.D(DATA_IN), .en(decoder_1_out26), .clk(CLK), .Q(x26_q));  // open: clr
  Register #(.width(32)) x27 (.D(DATA_IN), .en(decoder_1_out27), .clk(CLK), .Q(x27_q));  // open: clr
  Register #(.width(32)) x28 (.D(DATA_IN), .en(decoder_1_out28), .clk(CLK), .Q(x28_q));  // open: clr
  Register #(.width(32)) x29 (.D(DATA_IN), .en(decoder_1_out29), .clk(CLK), .Q(x29_q));  // open: clr
  Register #(.width(32)) x30 (.D(DATA_IN), .en(decoder_1_out30), .clk(CLK), .Q(x30_q));  // open: clr
  Register #(.width(32)) x31 (.D(DATA_IN), .en(decoder_1_out31), .clk(CLK), .Q(x31_q));  // open: clr
  Multiplexer #(.select(5), .width(32)) multiplexer_1 (
    .in0({32{1'b0}}), .in1(x1_q), .in2(x2_q), .in3(x3_q), .in4(x4_q), .in5(x5_q), .in6(x6_q), .in7(x7_q),
    .in8(x8_q), .in9(x9_q), .in10(x10_q), .in11(x11_q), .in12(x12_q), .in13(x13_q), .in14(x14_q),
    .in15(x15_q), .in16(x16_q), .in17(x17_q), .in18(undriven), .in19(x19_q), .in20(x20_q), .in21(x21_q),
    .in22(undriven_2), .in23(x23_q), .in24(x24_q), .in25(x25_q), .in26(x26_q), .in27(x27_q), .in28(x28_q),
    .in29(x29_q), .in30(x30_q), .in31(x31_q), .out(READ_1), .sel(ADR_1));
  Multiplexer #(.select(5), .width(32)) multiplexer_2 (
    .in0({32{1'b0}}), .in1(x1_q), .in2(x2_q), .in3(x3_q), .in4(x4_q), .in5(x5_q), .in6(x6_q), .in7(x7_q),
    .in8(x8_q), .in9(x9_q), .in10(x10_q), .in11(x11_q), .in12(x12_q), .in13(x13_q), .in14(x14_q),
    .in15(x15_q), .in16(x16_q), .in17(x17_q), .in18(undriven), .in19(x19_q), .in20(x20_q), .in21(x21_q),
    .in22(undriven_2), .in23(x23_q), .in24(x24_q), .in25(x25_q), .in26(x26_q), .in27(x27_q), .in28(x28_q),
    .in29(x29_q), .in30(x30_q), .in31(x31_q), .out(READ_2), .sel(ADR_2));
endmodule

module byte_adrr_ram (
  input  [31:0] WORD_ADDR,
  input  [2:0] READ_CTRL,
  input  CLK,
  input  [1:0] WRITE_CTRL,
  input  [31:0] DATA_IN,
  output [31:0] RAM_OUT
);

  wire nand_1_out, nor_1_out, not_1_out;
  wire [7:0] ram_1_dout, ram_2_dout, ram_3_dout, ram_4_dout;
  wire [23:0] adder_1_out, adder_2_out, adder_3_out, bit_extender_1_out;
  wire [31:0] bit_extender_2_out, bit_extender_3_out, bit_extender_4_out, bit_extender_5_out;

  nand nand_1 (nand_1_out, WRITE_CTRL[0], WRITE_CTRL[1]);
  not not_1 (not_1_out, WRITE_CTRL[1]);
  nor nor_1 (nor_1_out, WRITE_CTRL[0], WRITE_CTRL[1]);
  Bit_Extender #(.in_width(32), .out_width(24)) bit_extender_1 (.in(WORD_ADDR), .out(bit_extender_1_out));
  Adder #(.width(24)) adder_1 (.a(bit_extender_1_out), .b(24'h1), .out(adder_1_out));  // open: cin, cout
  Adder #(.width(24)) adder_2 (.a(adder_1_out), .b(24'h1), .out(adder_2_out));  // open: cin, cout
  Adder #(.width(24)) adder_3 (.a(adder_2_out), .b(24'h1), .out(adder_3_out));  // open: cin, cout
  RAM #(.addrWidth(24), .enables("line")) ram_1 (
    .addr(bit_extender_1_out), .we(nand_1_out), .clk(CLK), .din(DATA_IN[7:0]), .dout(ram_1_dout));
  RAM #(.addrWidth(24), .enables("line")) ram_2 (
    .addr(adder_1_out), .we(not_1_out), .clk(CLK), .din(DATA_IN[15:8]), .dout(ram_2_dout));
  RAM #(.addrWidth(24), .enables("line")) ram_3 (
    .addr(adder_2_out), .we(nor_1_out), .clk(CLK), .din(DATA_IN[23:16]), .dout(ram_3_dout));
  RAM #(.addrWidth(24), .enables("line")) ram_4 (
    .addr(adder_3_out), .we(nor_1_out), .clk(CLK), .din(DATA_IN[31:24]), .dout(ram_4_dout));
  assign bit_extender_2_out = {{24{ram_1_dout[7]}}, ram_1_dout};  // Bit_Extender bit_extender_2
  assign bit_extender_3_out = {{24{1'b0}}, ram_1_dout};  // Bit_Extender bit_extender_3
  assign bit_extender_4_out = {{16{ram_2_dout[7]}}, {ram_2_dout, ram_1_dout}};  // Bit_Extender bit_extender_4
  assign bit_extender_5_out = {{16{1'b0}}, {ram_2_dout, ram_1_dout}};  // Bit_Extender bit_extender_5
  Multiplexer #(.select(3), .width(32)) multiplexer_1 (
    .in0({ram_4_dout, ram_3_dout, ram_2_dout, ram_1_dout}), .in2(bit_extender_5_out),
    .in3(bit_extender_4_out), .in4(bit_extender_3_out), .in5(bit_extender_2_out), .out(RAM_OUT),
    .sel(READ_CTRL));  // open: in1, in6, in7
endmodule

module control_unit (
  input  [31:0] INSTR,
  input  [2:0] ALU_FLAGS,
  output [2:0] WRITE_DATA_SELECT,
  output [1:0] RAM_WRITE_TYPE,
  output [2:0] RAM_READ_TYPE,
  output [3:0] ALU_OP_TYPE,
  output ALU_CMP_TYPE,
  output ALU_B_OPERAND_SELECT,
  output REG_WRITE,
  output [2:0] IMM_TYPE_SELECT,
  output PC_SELECT
);

  PLA #(.in_width(20), .out_width(19), .\table ("0000011000xxxxxxxxxx 0000110001010111101\n0000011001xxxxxxxxxx 0000110001001111101\n0000011010xxxxxxxxxx 0000110001000011101\n0000011100xxxxxxxxxx 0000110001010011101\n0000011101xxxxxxxxxx 0000110001001011101\n0010011000xxxxxxxxxx 0000110001000011011\n00100110010000000xxx 0000110001100011011\n0010011010xxxxxxxxxx 0000110001100011010\n0010011011xxxxxxxxxx 0000111001100011010\n0010011100xxxxxxxxxx 0000110010100011011\n00100111010000000xxx 0000110010000011011\n00100111010100000xxx 0000110010100011011\n0010011110xxxxxxxxxx 0000110011100011011\n0010011111xxxxxxxxxx 0000110000100011011\n0010111xxxxxxxxxxxxx 0010100000000011111\n0100011000xxxxxxxxxx 0100010001000010000\n0100011001xxxxxxxxxx 0100010001000001000\n0100011010xxxxxxxxxx 0100010001000000000\n01100110000000000xxx 0000100001000011011\n01100110000100000xxx 0000100011000011011\n01100110010000000xxx 0000100001100011011\n01100110100000000xxx 0000100000000011010\n01100110110000000xxx 0000101000000011010\n01100111000000000xxx 0000100000000011011\n01100111010000000xxx 0000100010000011011\n01100111010100000xxx 0000100010100011011\n01100111100000000xxx 0000100011100011011\n01100111110000000xxx 0000100000100011011\n0110111xxxxxxxxxxxxx 0010100000000011100\n1100011000xxxxxxxxx1 1111000000000011000\n1100011000xxxxxxxxx0 0111000000000011000\n1100011001xxxxxxxxx0 1111000000000011000\n1100011100xxxxxxx1xx 1111000000000011000\n1100011100xxxxxxx0xx 0111000000000011000\n1100011101xxxxxxx0x1 1111000000000011000\n1100011101xxxxxxx1x0 1111000000000011000\n1100011101xxxxxxx1x1 1111000000000011000\n1100011101xxxxxxx0x0 0111000000000011000\n1100011110xxxxxxx1xx 1111001000000011000\n1100011110xxxxxxx0xx 0111001000000011000\n1100011111xxxxxxx1x0 1111001000000011000\n1100011111xxxxxxx0x1 1111001000000011000\n1100011111xxxxxxx1x1 1111001000000011000\n1100011111xxxxxxx0x0 0111001000000011000\n1100111xxxxxxxxxxxxx 1000110001000011110\n1101111xxxxxxxxxxxxx 1001110000000011110\n01100110000000001xxx 0000100100000000011\n01100111000000001xxx 0000100100100000011\n01100111010000001xxx 0000100101000000011\n01100111100000001xxx 0000100101100000011\n01100111110000001xxx 0000100110000000011")) pla_1 (
    .in({INSTR[6:0], INSTR[14:12], INSTR[31:25], ALU_FLAGS}),
    .out({PC_SELECT, IMM_TYPE_SELECT, REG_WRITE, ALU_B_OPERAND_SELECT, ALU_CMP_TYPE, ALU_OP_TYPE, RAM_READ_TYPE, RAM_WRITE_TYPE, WRITE_DATA_SELECT}));

  // Notes on the sheet:
  //   op
  //   func3
  //   func7
endmodule

module imm_select (
  input  [31:0] INSTR,
  input  [2:0] control,
  output [31:0] IMM
);

  wire [31:0] bit_extender_1_out, bit_extender_2_out, bit_extender_3_out, bit_extender_4_out;

  assign bit_extender_1_out = {{11{INSTR[31]}}, {INSTR[31], INSTR[19:12], INSTR[20], INSTR[30:21], 1'b0}};  // Bit_Extender bit_extender_1
  assign bit_extender_2_out = {{20{INSTR[31]}}, INSTR[31:20]};  // Bit_Extender bit_extender_2
  assign bit_extender_3_out = {{20{INSTR[31]}}, {INSTR[31:25], INSTR[11:7]}};  // Bit_Extender bit_extender_3
  assign bit_extender_4_out = {{19{INSTR[31]}}, {INSTR[31], INSTR[7], INSTR[30:25], INSTR[11:8], 1'b0}};  // Bit_Extender bit_extender_4
  Multiplexer #(.select(3), .width(32)) multiplexer_1 (
    .in0(bit_extender_2_out), .in1(bit_extender_1_out), .in2({INSTR[31:12], {12{1'b0}}}),
    .in4(bit_extender_3_out), .in7(bit_extender_4_out), .out(IMM), .sel(control));  // open: in3, in5, in6

  // Notes on the sheet:
  //   I_TYPE_IMMEDIATE
  //   S_TYPE_IMMEDIATE
  //   U_TYPE_IMMEDIATE
  //   J_TYPE_IMMEDIATE
  //   B_TYPE_IMMEDIATE
endmodule
