// Logisim project cpu_32_pipelined.circ as structural Verilog: 7 circuits, main circuit main
module main (
);

  wire and_1_out, and_2_out, and_3_out, and_4_out, and_5_out, and_6_out, and_7_out, and_8_out, CLK_out,
       control_unit_1_pc_select_b_operand_select, hazard_unit_1_flush_decode, hazard_unit_1_flush_exe,
       hazard_unit_1_flush_mem, hazard_unit_1_stall_decode, hazard_unit_1_stall_fetch, not_1_out, not_2_out,
       not_3_out, not_4_out, or_1_out, or_2_out, or_3_out, or_4_out, or_5_out, or_6_out, or_7_out, or_8_out,
       or_9_out, or_10_out, or_11_out, or_12_out, register_1_q, RESET_out;
  wire [1:0] control_unit_1_ram_write_type, hazard_unit_1_forward_a, hazard_unit_1_forward_b;
  wire [2:0] alu_1_eq, control_unit_1_imm_type_select, control_unit_1_ram_read_type,
       control_unit_1_write_data_select, register_2_q_2, undriven;
  wire [3:0] control_unit_1_alu_op_type, register_4_q;
  wire [4:0] EXE_REG_WRITE_ADRR_q, EXE_RS1_q, EXE_RS2_q, MEM_REG_WRITE_ADR_q, WRITE_REG_WRITE_ADR_q;
  wire [9:0] register_3_q;
  wire [24:0] register_2_q;
  wire [24:12] control_unit_1_alu_cmp_type;
  wire [31:0] adder_1_out, adder_2_out, alu_1_alu_result, bit_extender_1_out, DATA_MEMORY_ram_out,
       DEC_INSTR_q, DEC_PC4_q, DEC_PC_q, EXE_IM_q, EXE_PC_q, EXE_RD1_q, EXE_RD2_q, EXEE_PC4_q,
       imm_select_1_imm, INSTR_MEMORY_ram_out, MEM_ALU_RES_q, MEM_IM_q, MEM_PC4_q, MEM_PCIMM_q,
       MEM_RAM_DATA_IN_q, MEM_SIGN_EXT_q, multiplexer_1_out, multiplexer_2_out, multiplexer_3_out,
       multiplexer_4_out, multiplexer_5_out, multiplexer_6_out, PC_q, reg_file_1_read_1, reg_file_1_read_2,
       WRITE_ALU_RES_q, WRITE_IMM_q, WRITE_PC4_q, WRITE_PCIMM_q, WRITE_SIGN_EXT_q, WRITRE_RAM_OUT_q;

  Button RESET (.out(RESET_out));
  Clock CLK (.out(CLK_out));
  Adder #(.width(32)) adder_1 (.a(PC_q), .b(32'h4), .out(adder_1_out));  // open: cin, cout
  Multiplexer #(.width(32)) multiplexer_1 (
    .in0(adder_1_out), .in1(multiplexer_5_out), .out(multiplexer_1_out), .sel(or_1_out));
  Register #(.width(32)) PC (.D(multiplexer_1_out), .en(not_3_out), .clk(CLK_out), .Q(PC_q), .clr(RESET_out));
  or or_1 (or_1_out, or_3_out, register_2_q[24]);
  byte_adrr_ram INSTR_MEMORY (
    .READ_CTRL(3'b001), .WRITE_CTRL(2'b00), .WORD_ADDR(PC_q), .RAM_OUT(INSTR_MEMORY_ram_out));  // open: DATA_IN, CLK
  Register #(.width(32)) DEC_INSTR (
    .D(INSTR_MEMORY_ram_out), .en(not_4_out), .clk(CLK_out), .Q(DEC_INSTR_q), .clr(or_2_out));
  Register #(.width(32)) DEC_PC (.D(PC_q), .en(not_4_out), .clk(CLK_out), .Q(DEC_PC_q), .clr(or_2_out));
  Register #(.width(32)) DEC_PC4 (.D(adder_1_out), .en(not_4_out), .clk(CLK_out), .Q(DEC_PC4_q), .clr(or_2_out));
  or or_2 (or_2_out, hazard_unit_1_flush_decode, RESET_out);
  or or_3 (or_3_out, or_5_out, or_4_out);
  or or_4 (or_4_out, and_1_out, and_2_out, and_3_out);
  or or_5 (or_5_out, and_4_out, and_5_out, and_6_out);
  and and_1 (and_1_out, or_6_out, register_2_q[20]);
  and and_2 (and_2_out, register_2_q[19], alu_1_eq[2]);
  and and_3 (and_3_out, register_2_q[18], or_6_out);
  control_unit control_unit_1 (
    .INSTR(DEC_INSTR_q), .PC_SELECT_B_OPERAND_SELECT(control_unit_1_pc_select_b_operand_select),
    .WRITE_DATA_SELECT(control_unit_1_write_data_select), .RAM_WRITE_TYPE(control_unit_1_ram_write_type),
    .RAM_READ_TYPE(control_unit_1_ram_read_type), .ALU_OP_TYPE(control_unit_1_alu_op_type),
    .ALU_CMP_TYPE(control_unit_1_alu_cmp_type[12]), .ALU_B_OPERAND_SELECT(control_unit_1_alu_cmp_type[13]),
    .REG_WRITE(control_unit_1_alu_cmp_type[14]), .IMM_TYPE_SELECT(control_unit_1_imm_type_select),
    .BGEU(control_unit_1_alu_cmp_type[18]), .BLTU(control_unit_1_alu_cmp_type[19]),
    .BGE(control_unit_1_alu_cmp_type[20]), .BLT(control_unit_1_alu_cmp_type[21]),
    .BNE(control_unit_1_alu_cmp_type[22]), .BEQ(control_unit_1_alu_cmp_type[23]),
    .JUMP(control_unit_1_alu_cmp_type[24]));
  and and_4 (and_4_out, register_2_q[23], and_7_out);
  and and_5 (and_5_out, register_2_q[22], not_1_out);
  and and_6 (and_6_out, register_2_q[21], alu_1_eq[2]);
  and and_7 (and_7_out, register_2_q[23], alu_1_eq[0]);
  not not_1 (not_1_out, alu_1_eq[0]);
  not not_2 (not_2_out, CLK_out);
  Register #(.width(1)) register_1 (
    .D(control_unit_1_pc_select_b_operand_select), .en(1'b1), .clk(CLK_out), .Q(register_1_q), .clr(or_7_out));
  Register #(.width(25)) register_2 (
    .D({control_unit_1_alu_cmp_type[24:18], control_unit_1_imm_type_select, control_unit_1_alu_cmp_type[14:12], control_unit_1_alu_op_type, control_unit_1_ram_read_type, control_unit_1_ram_write_type, control_unit_1_write_data_select}),
    .en(1'b1), .clk(CLK_out), .Q({register_2_q[24:8], register_2_q_2, register_2_q[4:0]}), .clr(or_7_out));
  or or_6 (or_6_out, alu_1_eq[1], alu_1_eq[0]);
  or or_7 (or_7_out, and_8_out, RESET_out);
  reg_file reg_file_1 (
    .ADR_2(DEC_INSTR_q[24:20]), .RESET(RESET_out), .CLK(not_2_out), .WRITE_ENABLE(register_4_q[3]),
    .WRITE_ADR(WRITE_REG_WRITE_ADR_q), .DATA_IN(multiplexer_6_out), .ADR_1(DEC_INSTR_q[19:15]),
    .READ_2(reg_file_1_read_2), .READ_1(reg_file_1_read_1));
  imm_select imm_select_1 (.INSTR(DEC_INSTR_q), .control(undriven), .IMM(imm_select_1_imm));
  or or_8 (or_8_out, register_2_q[18], register_2_q[19]);
  or or_9 (or_9_out, register_2_q[20], register_2_q[21]);
  or or_10 (or_10_out, register_2_q[22], register_2_q[23]);
  Register #(.width(32)) EXE_RD1 (.D(reg_file_1_read_1), .en(1'b1), .clk(CLK_out), .Q(EXE_RD1_q), .clr(or_7_out));
  Register #(.width(32)) EXE_RD2 (.D(reg_file_1_read_2), .en(1'b1), .clk(CLK_out), .Q(EXE_RD2_q), .clr(or_7_out));
  Register #(.width(32)) EXE_IM (.D(imm_select_1_imm), .en(1'b1), .clk(CLK_out), .Q(EXE_IM_q), .clr(or_7_out));
  Register #(.width(32)) EXE_PC (.D(DEC_PC_q), .en(1'b1), .clk(CLK_out), .Q(EXE_PC_q), .clr(or_7_out));
  Register #(.width(5)) EXE_REG_WRITE_ADRR (
    .D(DEC_INSTR_q[11:7]), .en(1'b1), .clk(CLK_out), .Q(EXE_REG_WRITE_ADRR_q), .clr(or_7_out));
  Register #(.width(32)) EXEE_PC4 (.D(DEC_PC4_q), .en(1'b1), .clk(CLK_out), .Q(EXEE_PC4_q), .clr(or_7_out));
  Register #(.width(5)) EXE_RS1 (.D(DEC_INSTR_q[19:15]), .en(1'b1), .clk(CLK_out), .Q(EXE_RS1_q), .clr(or_7_out));
  Register #(.width(5)) EXE_RS2 (.D(DEC_INSTR_q[24:20]), .en(1'b1), .clk(CLK_out), .Q(EXE_RS2_q), .clr(or_7_out));
  and and_8 (and_8_out, CLK_out, hazard_unit_1_flush_exe);
  or or_11 (or_11_out, or_8_out, or_9_out, or_10_out);
  Adder #(.width(32)) adder_2 (.a(EXE_IM_q), .b(EXE_PC_q), .out(adder_2_out));  // open: cin, cout
  Register #(.width(10)) register_3 (
    .D({1'b0, register_2_q[14], register_2_q_2, register_2_q[4:0]}), .en(1'b1), .clk(CLK_out),
    .Q(register_3_q), .clr(or_12_out));
  Multiplexer #(.select(2), .width(32)) multiplexer_2 (
    .in0(EXE_RD1_q), .in2(multiplexer_6_out), .in3(MEM_ALU_RES_q), .out(multiplexer_2_out),
    .sel(hazard_unit_1_forward_a));  // open: in1
  Multiplexer #(.select(2), .width(32)) multiplexer_3 (
    .in0(EXE_RD2_q), .in2(multiplexer_6_out), .in3(MEM_ALU_RES_q), .out(multiplexer_3_out),
    .sel(hazard_unit_1_forward_b));  // open: in1
  Clock clock_1 ();  // open: out
  Multiplexer #(.width(32)) multiplexer_4 (
    .in0(multiplexer_3_out), .in1(EXE_IM_q), .out(multiplexer_4_out), .sel(register_2_q[13]));
  assign bit_extender_1_out = {{31{alu_1_eq[2]}}, alu_1_eq[2]};  // Bit_Extender bit_extender_1
  alu alu_1 (
    .in_2(multiplexer_2_out), .in_3(multiplexer_4_out), .ALU_CMPR_CTRL(register_2_q[12]),
    .ALU_OP_CTRL(register_2_q[11:8]), .ALU_CMP_ENABLE(or_11_out), .GT(alu_1_eq[1]), .EQ(alu_1_eq[0]),
    .LT(alu_1_eq[2]), .ALU_RESULT(alu_1_alu_result));
  Multiplexer #(.width(32)) multiplexer_5 (
    .in0(adder_2_out), .in1(alu_1_alu_result), .out(multiplexer_5_out), .sel(register_1_q));
  hazard_unit hazard_unit_1 (
    .CLK(CLK_out), .PC_SELECT(or_1_out), .MEM_REG_WRITE(register_3_q[8]), .RD_E(EXE_REG_WRITE_ADRR_q),
    .RS2_D(DEC_INSTR_q[19:15]), .EXE_RS2(EXE_RS2_q), .RS1_D(DEC_INSTR_q[24:20]),
    .RAM_SELECT_SIGNAL(register_2_q_2), .MEM_REG_WRITE_ADR(MEM_REG_WRITE_ADR_q),
    .WRITE_REG_WRITE_ADR(WRITE_REG_WRITE_ADR_q), .WRITE_REG_WRITE(register_4_q[3]), .EXE_RS1(EXE_RS1_q),
    .FORWARD_A(hazard_unit_1_forward_a), .FORWARD_B(hazard_unit_1_forward_b),
    .FLUSH_EXE(hazard_unit_1_flush_exe), .STALL_FETCH(hazard_unit_1_stall_fetch),
    .STALL_DECODE(hazard_unit_1_stall_decode), .FLUSH_DECODE(hazard_unit_1_flush_decode),
    .FLUSH_MEM(hazard_unit_1_flush_mem));
  not not_3 (not_3_out, hazard_unit_1_stall_fetch);
  not not_4 (not_4_out, hazard_unit_1_stall_decode);
  Register #(.width(32)) MEM_SIGN_EXT (
    .D(bit_extender_1_out), .en(1'b1), .clk(CLK_out), .Q(MEM_SIGN_EXT_q), .clr(or_12_out));
  Register #(.width(32)) MEM_ALU_RES (
    .D(alu_1_alu_result), .en(1'b1), .clk(CLK_out), .Q(MEM_ALU_RES_q), .clr(or_12_out));
  Register #(.width(32)) MEM_RAM_DATA_IN (
    .D(multiplexer_3_out), .en(1'b1), .clk(CLK_out), .Q(MEM_RAM_DATA_IN_q), .clr(or_12_out));
  Register #(.width(32)) MEM_IM (.D(EXE_IM_q), .en(1'b1), .clk(CLK_out), .Q(MEM_IM_q), .clr(or_12_out));
  Register #(.width(32)) MEM_PCIMM (.D(adder_2_out), .en(1'b1), .clk(CLK_out), .Q(MEM_PCIMM_q), .clr(or_12_out));
  Register #(.width(5)) MEM_REG_WRITE_ADR (
    .D(EXE_REG_WRITE_ADRR_q), .en(1'b1), .clk(CLK_out), .Q(MEM_REG_WRITE_ADR_q), .clr(or_12_out));
  Register #(.width(32)) MEM_PC4 (.D(EXEE_PC4_q), .en(1'b1), .clk(CLK_out), .Q(MEM_PC4_q), .clr(or_12_out));
  Register #(.width(4)) register_4 (
    .D({register_3_q[8], register_3_q[2:0]}), .en(1'b1), .clk(CLK_out), .Q(register_4_q), .clr(RESET_out));
  or or_12 (or_12_out, RESET_out, hazard_unit_1_flush_mem);
  byte_adrr_ram DATA_MEMORY (
    .READ_CTRL(register_3_q[7:5]), .DATA_IN(MEM_RAM_DATA_IN_q), .WRITE_CTRL(register_3_q[4:3]),
    .WORD_ADDR(MEM_ALU_RES_q), .CLK(CLK_out), .RAM_OUT(DATA_MEMORY_ram_out));
  Register #(.width(32)) WRITE_SIGN_EXT (
    .D(MEM_SIGN_EXT_q), .en(1'b1), .clk(CLK_out), .Q(WRITE_SIGN_EXT_q));  // open: clr
  Register #(.width(32)) WRITRE_RAM_OUT (
    .D(DATA_MEMORY_ram_out), .en(1'b1), .clk(CLK_out), .Q(WRITRE_RAM_OUT_q), .clr(RESET_out));
  Register #(.width(32)) WRITE_ALU_RES (
    .D(MEM_ALU_RES_q), .en(1'b1), .clk(CLK_out), .Q(WRITE_ALU_RES_q), .clr(RESET_out));
  Register #(.width(32)) WRITE_IMM (.D(MEM_IM_q), .en(1'b1), .clk(CLK_out), .Q(WRITE_IMM_q));  // open: clr
  Register #(.width(32)) WRITE_PCIMM (.D(MEM_PCIMM_q), .en(1'b1), .clk(CLK_out), .Q(WRITE_PCIMM_q), .clr(RESET_out));
  Register #(.width(5)) WRITE_REG_WRITE_ADR (
    .D(MEM_REG_WRITE_ADR_q), .en(1'b1), .clk(CLK_out), .Q(WRITE_REG_WRITE_ADR_q), .clr(RESET_out));
  Register #(.width(32)) WRITE_PC4 (.D(MEM_PC4_q), .en(1'b1), .clk(CLK_out), .Q(WRITE_PC4_q), .clr(RESET_out));
  Multiplexer #(.select(3), .width(32)) multiplexer_6 (
    .in2(WRITE_SIGN_EXT_q), .in3(WRITE_ALU_RES_q), .in4(WRITE_IMM_q), .in5(WRITRE_RAM_OUT_q),
    .in6(WRITE_PC4_q), .in7(WRITE_PCIMM_q), .out(multiplexer_6_out), .sel(register_4_q[2:0]));  // open: in0, in1

  // Notes on the sheet:
  //   F3_32P :)
  //   PC
  //   RD
  //   RS1
  //   RS2
  //   LT
  //   ALU_RESULT
  //   PC+4
  //   IM
  //   PC+IM
endmodule

module alu (
  input  [3:0] ALU_OP_CTRL,
  input  [31:0] in_2,
  input  [31:0] in_3,
  input  ALU_CMPR_CTRL,
  input  ALU_CMP_ENABLE,
  output [31:0] ALU_RESULT,
  output GT,
  output EQ,
  output LT
);

  wire comparator_1_eq, comparator_1_gt, comparator_1_lt, comparator_2_eq, comparator_2_gt, comparator_2_lt,
       multiplexer_1_out, multiplexer_2_out, multiplexer_3_out, not_1_out;
  wire [4:0] bit_extender_1_out, bit_extender_2_out, bit_extender_3_out;
  wire [31:0] adder_1_out, and_1_out, divider_1_out, divider_1_rem, divider_2_out, divider_2_rem,
       multiplier_1_cout, multiplier_1_out, or_1_out, shifter_1_out, shifter_2_out, shifter_3_out,
       subtractor_1_out, xor_1_out;

  assign or_1_out = in_3 | in_2;  // OR_Gate or_1, 32 bits wide
  assign xor_1_out = in_3 ^ in_2;  // XOR_Gate xor_1, 32 bits wide
  assign and_1_out = in_3 & in_2;  // AND_Gate and_1, 32 bits wide
  Adder #(.width(32)) adder_1 (.a(in_2), .b(in_3), .out(adder_1_out));  // open: cin, cout
  Shifter #(.width(32)) shifter_1 (.in(in_2), .\dist (bit_extender_1_out), .out(shifter_1_out));
  Bit_Extender #(.in_width(32), .out_width(5)) bit_extender_1 (.in(in_3), .out(bit_extender_1_out));
  Shifter #(.shift("lr"), .width(32)) shifter_2 (.in(in_2), .\dist (bit_extender_2_out), .out(shifter_2_out));
  Bit_Extender #(.in_width(32), .out_width(5)) bit_extender_2 (.in(in_3), .out(bit_extender_2_out));
  Shifter #(.shift("ar"), .width(32)) shifter_3 (.in(in_2), .\dist (bit_extender_3_out), .out(shifter_3_out));
  Bit_Extender #(.in_width(32), .out_width(5)) bit_extender_3 (.in(in_3), .out(bit_extender_3_out));
  Subtractor #(.width(32)) subtractor_1 (.a(in_2), .b(in_3), .out(subtractor_1_out));  // open: bin, bout
  Comparator #(.width(32)) comparator_1 (
    .a(in_2), .b(in_3), .gt(comparator_1_gt), .eq(comparator_1_eq), .lt(comparator_1_lt));
  Comparator #(.mode("unsigned"), .width(32)) comparator_2 (
    .a(in_2), .b(in_3), .gt(comparator_2_gt), .eq(comparator_2_eq), .lt(comparator_2_lt));
  Multiplexer multiplexer_1 (
    .in0(comparator_1_gt), .in1(comparator_2_gt), .out(multiplexer_1_out), .sel(ALU_CMPR_CTRL));
  Multiplexer multiplexer_2 (
    .in0(comparator_1_eq), .in1(comparator_2_eq), .out(multiplexer_2_out), .sel(ALU_CMPR_CTRL));
  Multiplexer multiplexer_3 (
    .in0(comparator_1_lt), .in1(comparator_2_lt), .out(multiplexer_3_out), .sel(ALU_CMPR_CTRL));
  Multiplier #(.mode("twosComplement"), .width(32)) multiplier_1 (
    .a(in_3), .b(in_2), .out(multiplier_1_out), .cout(multiplier_1_cout));  // open: cin
  Divider #(.width(32)) divider_1 (
    .a(in_2), .b(in_3), .out(divider_1_out), .upper(multiplier_1_cout), .rem(divider_1_rem));
  Divider #(.mode("twosComplement"), .width(32)) divider_2 (
    .a(in_2), .b(in_3), .out(divider_2_out), .rem(divider_2_rem));  // open: upper
  assign GT = ALU_CMP_ENABLE ? multiplexer_1_out : 1'bz;  // Controlled_Buffer controlled_buffer_1
  assign EQ = ALU_CMP_ENABLE ? multiplexer_2_out : 1'bz;  // Controlled_Buffer controlled_buffer_2
  assign LT = ALU_CMP_ENABLE ? multiplexer_3_out : 1'bz;  // Controlled_Buffer controlled_buffer_3
  not not_1 (not_1_out, ALU_CMP_ENABLE);
  assign LT = not_1_out ? 1'b0 : 1'bz;  // Controlled_Buffer controlled_buffer_4
  assign EQ = not_1_out ? 1'b0 : 1'bz;  // Controlled_Buffer controlled_buffer_5
  assign GT = not_1_out ? 1'b0 : 1'bz;  // Controlled_Buffer controlled_buffer_6
  Multiplexer #(.select(4), .width(32)) multiplexer_4 (
    .in0(xor_1_out), .in1(and_1_out), .in2(adder_1_out), .in3(shifter_1_out), .in4(shifter_2_out),
    .in5(shifter_3_out), .in6(subtractor_1_out), .in7(or_1_out), .in8(multiplier_1_out), .in9(divider_2_out),
    .in10(divider_1_out), .in11(divider_2_rem), .in12(divider_1_rem), .out(ALU_RESULT), .sel(ALU_OP_CTRL));  // open: in13, in14, in15

  // Notes on the sheet:
  //   A+B
  //   A-B
endmodule

module reg_file (
  input  [4:0] ADR_2,
  input  [4:0] ADR_1,
  input  WRITE_ENABLE,
  input  [4:0] WRITE_ADR,
  input  [31:0] DATA_IN,
  input  CLK,
  input  RESET,
  output [31:0] READ_1,
  output [31:0] READ_2
);

  wire decoder_1_out1, decoder_1_out2, decoder_1_out3, decoder_1_out4, decoder_1_out5, decoder_1_out6,
       decoder_1_out7, decoder_1_out8, decoder_1_out9, decoder_1_out10, decoder_1_out11, decoder_1_out12,
       decoder_1_out13, decoder_1_out14, decoder_1_out15, decoder_1_out16, decoder_1_out17, decoder_1_out18,
       decoder_1_out19, decoder_1_out20, decoder_1_out21, decoder_1_out22, decoder_1_out23, decoder_1_out24,
       decoder_1_out25, decoder_1_out26, decoder_1_out27, decoder_1_out28, decoder_1_out29, decoder_1_out30,
       decoder_1_out31, undriven;
  wire [31:0] undriven_2, undriven_3, x1_q, x2_q, x3_q, x4_q, x5_q, x6_q, x7_q, x8_q, x9_q, x10_q, x11_q,
       x12_q, x13_q, x14_q, x15_q, x16_q, x17_q, x19_q, x20_q, x21_q, x23_q, x24_q, x25_q, x26_q, x27_q,
       x28_q, x29_q, x30_q, x31_q;

  Decoder #(.select(5)) decoder_1 (
    .out1(decoder_1_out1), .out2(decoder_1_out2), .out3(decoder_1_out3), .out4(decoder_1_out4),
    .out5(decoder_1_out5), .out6(decoder_1_out6), .out7(decoder_1_out7), .out8(decoder_1_out8),
    .out9(decoder_1_out9), .out10(decoder_1_out10), .out11(decoder_1_out11), .out12(decoder_1_out12),
    .out13(decoder_1_out13), .out14(decoder_1_out14), .out15(decoder_1_out15), .out16(decoder_1_out16),
    .out17(decoder_1_out17), .out18(decoder_1_out18), .out19(decoder_1_out19), .out20(decoder_1_out20),
    .out21(decoder_1_out21), .out22(decoder_1_out22), .out23(decoder_1_out23), .out24(decoder_1_out24),
    .out25(decoder_1_out25), .out26(decoder_1_out26), .out27(decoder_1_out27), .out28(decoder_1_out28),
    .out29(decoder_1_out29), .out30(decoder_1_out30), .out31(decoder_1_out31), .sel(WRITE_ADR),
    .en(WRITE_ENABLE));  // open: out0
  Register #(.width(32)) x1 (.D(DATA_IN), .en(decoder_1_out1), .clk(CLK), .Q(x1_q), .clr(RESET));
  Register #(.width(32)) x2 (.D(DATA_IN), .en(decoder_1_out2), .clk(CLK), .Q(x2_q), .clr(undriven));
  Register #(.width(32)) x3 (.D(DATA_IN), .en(decoder_1_out3), .clk(CLK), .Q(x3_q));  // open: clr
  Register #(.width(32)) x4 (.D(DATA_IN), .en(decoder_1_out4), .clk(CLK), .Q(x4_q), .clr(RESET));
  Register #(.width(32)) x5 (.D(DATA_IN), .en(decoder_1_out5), .clk(CLK), .Q(x5_q), .clr(RESET));
  Register #(.width(32)) x6 (.D(DATA_IN), .en(decoder_1_out6), .clk(CLK), .Q(x6_q), .clr(RESET));
  Register #(.width(32)) x7 (.D(DATA_IN), .en(decoder_1_out7), .clk(CLK), .Q(x7_q));  // open: clr
  Register #(.width(32)) x8 (.D(DATA_IN), .en(decoder_1_out8), .clk(CLK), .Q(x8_q));  // open: clr
  Register #(.width(32)) x9 (.D(DATA_IN), .en(decoder_1_out9), .clk(CLK), .Q(x9_q));  // open: clr
  Register #(.width(32)) x10 (.D(DATA_IN), .en(decoder_1_out10), .clk(CLK), .Q(x10_q));  // open: clr
  Register #(.width(32)) x11 (.D(DATA_IN), .en(decoder_1_out11), .clk(CLK), .Q(x11_q));  // open: clr
  Register #(.width(32)) x12 (.D(DATA_IN), .en(decoder_1_out12), .clk(CLK), .Q(x12_q));  // open: clr
  Register #(.width(32)) x13 (.D(DATA_IN), .en(decoder_1_out13), .clk(CLK), .Q(x13_q));  // open: clr
  Register #(.width(32)) x14 (.D(DATA_IN), .en(decoder_1_out14), .clk(CLK), .Q(x14_q));  // open: clr
  Register #(.width(32)) x15 (.D(DATA_IN), .en(decoder_1_out15), .clk(CLK), .Q(x15_q));  // open: clr
  Register #(.width(32)) x16 (.D(DATA_IN), .en(decoder_1_out16), .clk(CLK), .Q(x16_q));  // open: clr
  Register #(.width(32)) x17 (.D(DATA_IN), .en(decoder_1_out17), .clk(CLK), .Q(x17_q));  // open: clr
  Register #(.width(32)) x18 (.D(DATA_IN), .en(decoder_1_out18), .clk(CLK));  // open: Q, clr
  Register #(.width(32)) x19 (.D(DATA_IN), .en(decoder_1_out19), .clk(CLK), .Q(x19_q));  // open: clr
  Register #(.width(32)) x20 (.D(DATA_IN), .en(decoder_1_out20), .clk(CLK), .Q(x20_q));  // open: clr
  Register #(.width(32)) x21 (.D(DATA_IN), .en(decoder_1_out21), .clk(CLK), .Q(x21_q));  // open: clr
  Register #(.width(32)) x22 (.D(DATA_IN), .en(decoder_1_out22), .clk(CLK));  // open: Q, clr
  Register #(.width(32)) x23 (.D(DATA_IN), .en(decoder_1_out23), .clk(CLK), .Q(x23_q));  // open: clr
  Register #(.width(32)) x24 (.D(DATA_IN), .en(decoder_1_out24), .clk(CLK), .Q(x24_q));  // open: clr
  Register #(.width(32)) x25 (.D(DATA_IN), .en(decoder_1_out25), .clk(CLK), .Q(x25_q));  // open: clr
  Register #(.width(32)) x26 (.D(DATA_IN), .en(decoder_1_out26), .clk(CLK), .Q(x26_q));  // open: clr
  Register #(.width(32)) x27 (.D(DATA_IN), .en(decoder_1_out27), .clk(CLK), .Q(x27_q));  // open: clr
  Register #(.width(32)) x28 (.D(DATA_IN), .en(decoder_1_out28), .clk(CLK), .Q(x28_q));  // open: clr
  Register #(.width(32)) x29 (.D(DATA_IN), .en(decoder_1_out29), .clk(CLK), .Q(x29_q));  // open: clr
  Register #(.width(32)) x30 (.D(DATA_IN), .en(decoder_1_out30), .clk(CLK), .Q(x30_q));  // open: clr
  Register #(.width(32)) x31 (.D(DATA_IN), .en(decoder_1_out31), .clk(CLK), .Q(x31_q));  // open: clr
  Multiplexer #(.select(5), .width(32)) multiplexer_1 (
    .in0({32{1'b0}}), .in1(x1_q), .in2(x2_q), .in3(x3_q), .in4(x4_q), .in5(x5_q), .in6(x6_q), .in7(x7_q),
    .in8(x8_q), .in9(x9_q), .in10(x10_q), .in11(x11_q), .in12(x12_q), .in13(x13_q), .in14(x14_q),
    .in15(x15_q), .in16(x16_q), .in17(x17_q), .in18(undriven_2), .in19(x19_q), .in20(x20_q), .in21(x21_q),
    .in22(undriven_3), .in23(x23_q), .in24(x24_q), .in25(x25_q), .in26(x26_q), .in27(x27_q), .in28(x28_q),
    .in29(x29_q), .in30(x30_q), .in31(x31_q), .out(READ_1), .sel(ADR_1));
  Multiplexer #(.select(5), .width(32)) multiplexer_2 (
    .in0({32{1'b0}}), .in1(x1_q), .in2(x2_q), .in3(x3_q), .in4(x4_q), .in5(x5_q), .in6(x6_q), .in7(x7_q),
    .in8(x8_q), .in9(x9_q), .in10(x10_q), .in11(x11_q), .in12(x12_q), .in13(x13_q), .in14(x14_q),
    .in15(x15_q), .in16(x16_q), .in17(x17_q), .in18(undriven_2), .in19(x19_q), .in20(x20_q), .in21(x21_q),
    .in22(undriven_3), .in23(x23_q), .in24(x24_q), .in25(x25_q), .in26(x26_q), .in27(x27_q), .in28(x28_q),
    .in29(x29_q), .in30(x30_q), .in31(x31_q), .out(READ_2), .sel(ADR_2));
endmodule

module byte_adrr_ram (
  input  [31:0] WORD_ADDR,
  input  [2:0] READ_CTRL,
  input  CLK,
  input  [1:0] WRITE_CTRL,
  input  [31:0] DATA_IN,
  output [31:0] RAM_OUT
);

  wire and_1_out, or_1_out;
  wire [7:0] RAM_1_dout, RAM_2_dout, RAM_3_dout, RAM_4_dout;
  wire [23:0] adder_1_out, adder_2_out, adder_3_out, bit_extender_1_out;
  wire [31:0] bit_extender_2_out, bit_extender_3_out, bit_extender_4_out, bit_extender_5_out;

  or or_1 (or_1_out, WRITE_CTRL[0], WRITE_CTRL[1]);
  and and_1 (and_1_out, WRITE_CTRL[0], WRITE_CTRL[1]);
  Bit_Extender #(.in_width(32), .out_width(24)) bit_extender_1 (.in(WORD_ADDR), .out(bit_extender_1_out));
  Adder #(.width(24)) adder_1 (.a(bit_extender_1_out), .b(24'h1), .out(adder_1_out));  // open: cin, cout
  Adder #(.width(24)) adder_2 (.a(adder_1_out), .b(24'h1), .out(adder_2_out));  // open: cin, cout
  Adder #(.width(24)) adder_3 (.a(adder_2_out), .b(24'h1), .out(adder_3_out));  // open: cin, cout
  RAM #(.addrWidth(24), .enables("line")) RAM_1 (
    .addr(bit_extender_1_out), .we(or_1_out), .clk(CLK), .din(DATA_IN[7:0]), .dout(RAM_1_dout));
  RAM #(.addrWidth(24), .enables("line")) RAM_2 (
    .addr(adder_1_out), .we(WRITE_CTRL[0]), .clk(CLK), .din(DATA_IN[15:8]), .dout(RAM_2_dout));
  RAM #(.addrWidth(24), .enables("line")) RAM_3 (
    .addr(adder_2_out), .we(and_1_out), .clk(CLK), .din(DATA_IN[23:16]), .dout(RAM_3_dout));
  RAM #(.addrWidth(24), .enables("line")) RAM_4 (
    .addr(adder_3_out), .we(and_1_out), .clk(CLK), .din(DATA_IN[31:24]), .dout(RAM_4_dout));
  assign bit_extender_2_out = {{24{RAM_1_dout[7]}}, RAM_1_dout};  // Bit_Extender bit_extender_2
  assign bit_extender_3_out = {{24{1'b0}}, RAM_1_dout};  // Bit_Extender bit_extender_3
  assign bit_extender_4_out = {{16{RAM_2_dout[7]}}, {RAM_2_dout, RAM_1_dout}};  // Bit_Extender bit_extender_4
  assign bit_extender_5_out = {{16{1'b0}}, {RAM_2_dout, RAM_1_dout}};  // Bit_Extender bit_extender_5
  Multiplexer #(.select(3), .width(32)) multiplexer_1 (
    .in1({RAM_4_dout, RAM_3_dout, RAM_2_dout, RAM_1_dout}), .in2(bit_extender_5_out),
    .in3(bit_extender_4_out), .in4(bit_extender_3_out), .in5(bit_extender_2_out), .out(RAM_OUT),
    .sel(READ_CTRL));  // open: in0, in6, in7
endmodule

module control_unit (
  input  [31:0] INSTR,
  output PC_SELECT_B_OPERAND_SELECT,
  output [2:0] WRITE_DATA_SELECT,
  output [1:0] RAM_WRITE_TYPE,
  output [2:0] RAM_READ_TYPE,
  output [3:0] ALU_OP_TYPE,
  output ALU_CMP_TYPE,
  output ALU_B_OPERAND_SELECT,
  output REG_WRITE,
  output [2:0] IMM_TYPE_SELECT,
  output BGEU,
  output BLTU,
  output BGE,
  output BLT,
  output BNE,
  output BEQ,
  output JUMP
);

  PLA #(.in_width(17), .out_width(26), .\table ("0000011000xxxxxxx 00000000001100010101001010\n0000011001xxxxxxx 00000000001100010011001010\n0000011010xxxxxxx 00000000001100010001001010\n0000011100xxxxxxx 00000000001100010100001010\n0000011101xxxxxxx 00000000001100010010001010\n0010011000xxxxxxx 00000000001100010000000110\n00100110010000000 00000000001100011000000110\n0010011010xxxxxxx 00000000001100011000000100\n0010011011xxxxxxx 00000000001110011000000100\n0010011100xxxxxxx 00000000001100101000000110\n00100111010000000 00000000001100100000000110\n00100111010100000 00000000001100101000000110\n0010011110xxxxxxx 00000000001100111000000110\n0010011111xxxxxxx 00000000001100001000000110\n0010111xxxxxxxxxx 00000000101000000000001110\n0100011000xxxxxxx 00000001000100010000100000\n0100011001xxxxxxx 00000001000100010000010000\n0100011010xxxxxxx 00000001000100010000110000\n01100110000000000 00000000001000010000000110\n01100110000100000 00000000001000110000000110\n01100110010000000 00000000001000011000000110\n01100110100000000 00000000001000000000000100\n01100110110000000 00000000001010000000000100\n01100111000000000 00000000001000000000000110\n01100111010000000 00000000001000100000000110\n01100111010100000 00000000001000101000000110\n01100111100000000 00000000001000111000000110\n01100111110000000 00000000001000001000000110\n0110111xxxxxxxxxx 00000000101000000000001000\n1100011000xxxxxxx 01000001110000000000000000\n1100011001xxxxxxx 00100001110000000000000000\n1100011100xxxxxxx 00010001110000000000000000\n1100011101xxxxxxx 00001001110000000000000000\n1100011110xxxxxxx 00000101110010000000000000\n1100011111xxxxxxx 00000011110010000000000000\n1100111xxxxxxxxxx 10000000001100010000001101\n1101111xxxxxxxxxx 10000000011100000000001100\n01100110000000001 00000000001001000000000110\n01100111000000001 00000000001001001000000110\n01100111010000001 00000000001001010000000110\n01100111100000001 00000000001001011000000110\n01100111110000001 00000000001001100000000110")) pla_1 (
    .in({INSTR[6:0], INSTR[14:12], INSTR[31:25]}),
    .out({JUMP, BEQ, BNE, BLT, BGE, BLTU, BGEU, IMM_TYPE_SELECT, REG_WRITE, ALU_B_OPERAND_SELECT, ALU_CMP_TYPE, ALU_OP_TYPE, RAM_READ_TYPE, RAM_WRITE_TYPE, WRITE_DATA_SELECT, PC_SELECT_B_OPERAND_SELECT}));

  // Notes on the sheet:
  //   op
  //   func3
  //   func7
endmodule

module imm_select (
  input  [31:0] INSTR,
  input  [2:0] control,
  output [31:0] IMM
);

  wire [31:0] bit_extender_1_out, bit_extender_2_out, bit_extender_3_out, bit_extender_4_out;

  assign bit_extender_1_out = {{11{INSTR[31]}}, {INSTR[31], INSTR[19:12], INSTR[20], INSTR[30:21], 1'b0}};  // Bit_Extender bit_extender_1
  assign bit_extender_2_out = {{20{INSTR[31]}}, INSTR[31:20]};  // Bit_Extender bit_extender_2
  assign bit_extender_3_out = {{20{INSTR[31]}}, {INSTR[31:25], INSTR[11:7]}};  // Bit_Extender bit_extender_3
  assign bit_extender_4_out = {{19{INSTR[31]}}, {INSTR[31], INSTR[7], INSTR[30:25], INSTR[11:8], 1'b0}};  // Bit_Extender bit_extender_4
  Multiplexer #(.select(3), .width(32)) multiplexer_1 (
    .in0(bit_extender_2_out), .in1(bit_extender_1_out), .in2({INSTR[31:12], {12{1'b0}}}),
    .in4(bit_extender_3_out), .in7(bit_extender_4_out), .out(IMM), .sel(control));  // open: in3, in5, in6

  // Notes on the sheet:
  //   I_TYPE_IMMEDIATE
  //   S_TYPE_IMMEDIATE
  //   U_TYPE_IMMEDIATE
  //   J_TYPE_IMMEDIATE
  //   B_TYPE_IMMEDIATE
endmodule

module hazard_unit (
  input  [4:0] EXE_RS1,
  input  [4:0] MEM_REG_WRITE_ADR,
  input  MEM_REG_WRITE,
  input  [4:0] WRITE_REG_WRITE_ADR,
  input  WRITE_REG_WRITE,
  input  [4:0] EXE_RS2,
  input  [2:0] RAM_SELECT_SIGNAL,
  input  CLK,
  input  [4:0] RS1_D,
  input  [4:0] RD_E,
  input  [4:0] RS2_D,
  input  PC_SELECT,
  output [1:0] FORWARD_A,
  output [1:0] FORWARD_B,
  output FLUSH_EXE,
  output STALL_FETCH,
  output STALL_DECODE,
  output FLUSH_MEM,
  output FLUSH_DECODE
);

  wire and_1_out, and_2_out, and_3_out, and_4_out, and_5_out, and_6_out, and_7_out, and_8_out, and_9_out,
       and_10_out, and_11_out, and_13_out, and_14_out, and_15_out, and_16_out, and_17_out, and_18_out,
       comparator_1_eq, comparator_2_eq, comparator_3_eq, comparator_4_eq, comparator_5_eq, comparator_6_eq,
       comparator_7_eq, comparator_8_eq, comparator_9_eq, comparator_10_eq, comparator_11_eq,
       comparator_12_eq, comparator_13_eq, counter_1_carry, counter_2_carry, counter_3_carry, d_ff_1_q,
       d_ff_2_q, nor_1_out, nor_2_out, not_1_out, not_2_out, not_3_out, not_4_out, not_5_out, not_6_out,
       not_7_out, or_1_out, or_2_out, or_3_out, or_4_out, or_5_out, or_7_out;

  Comparator #(.mode("unsigned"), .width(3)) comparator_1 (
    .a(RAM_SELECT_SIGNAL), .b(3'b101), .eq(comparator_1_eq));  // open: gt, lt
  Comparator #(.mode("unsigned"), .width(3)) comparator_2 (
    .a(RAM_SELECT_SIGNAL), .b(3'b100), .eq(comparator_2_eq));  // open: gt, lt
  Comparator #(.mode("unsigned"), .width(3)) comparator_3 (
    .a(RAM_SELECT_SIGNAL), .b(3'b011), .eq(comparator_3_eq));  // open: gt, lt
  Comparator #(.mode("unsigned"), .width(3)) comparator_4 (
    .a(RAM_SELECT_SIGNAL), .b(3'b001), .eq(comparator_4_eq));  // open: gt, lt
  Comparator #(.mode("unsigned"), .width(3)) comparator_5 (
    .a(RAM_SELECT_SIGNAL), .b(3'b001), .eq(comparator_5_eq));  // open: gt, lt
  Comparator #(.mode("unsigned"), .width(5)) comparator_6 (
    .a(EXE_RS1), .b(MEM_REG_WRITE_ADR), .eq(comparator_6_eq));  // open: gt, lt
  Comparator #(.mode("unsigned"), .width(5)) comparator_7 (
    .a(EXE_RS1), .b({5{1'b0}}), .eq(comparator_7_eq));  // open: gt, lt
  Comparator #(.mode("unsigned"), .width(5)) comparator_8 (
    .a(EXE_RS1), .b(WRITE_REG_WRITE_ADR), .eq(comparator_8_eq));  // open: gt, lt
  Comparator #(.mode("unsigned"), .width(5)) comparator_9 (
    .a(EXE_RS2), .b(MEM_REG_WRITE_ADR), .eq(comparator_9_eq));  // open: gt, lt
  Comparator #(.mode("unsigned"), .width(5)) comparator_10 (
    .a(EXE_RS2), .b({5{1'b0}}), .eq(comparator_10_eq));  // open: gt, lt
  Comparator #(.mode("unsigned"), .width(5)) comparator_11 (
    .a(EXE_RS2), .b(WRITE_REG_WRITE_ADR), .eq(comparator_11_eq));  // open: gt, lt
  or or_1 (or_1_out, comparator_1_eq, comparator_2_eq);
  or or_2 (or_2_out, comparator_3_eq, comparator_4_eq);
  Comparator #(.mode("unsigned"), .width(5)) comparator_12 (
    .a(RS1_D), .b(RD_E), .eq(comparator_12_eq));  // open: gt, lt
  Comparator #(.mode("unsigned"), .width(5)) comparator_13 (
    .a(RD_E), .b(RS2_D), .eq(comparator_13_eq));  // open: gt, lt
  or or_3 (or_3_out, or_1_out, or_2_out);
  and and_1 (and_1_out, comparator_6_eq, MEM_REG_WRITE);
  not not_1 (not_1_out, comparator_7_eq);
  and and_2 (and_2_out, comparator_8_eq, WRITE_REG_WRITE);
  and and_3 (and_3_out, comparator_9_eq, MEM_REG_WRITE);
  not not_2 (not_2_out, comparator_10_eq);
  and and_4 (and_4_out, comparator_11_eq, WRITE_REG_WRITE);
  or or_4 (or_4_out, or_3_out, comparator_5_eq);
  and and_5 (and_5_out, or_4_out, or_5_out);
  or or_5 (or_5_out, comparator_12_eq, comparator_13_eq);
  and and_6 (and_6_out, and_1_out, not_1_out);
  and and_7 (and_7_out, and_2_out, not_1_out);
  and and_8 (and_8_out, and_3_out, not_2_out);
  and and_9 (and_9_out, not_2_out, and_4_out);
  not not_3 (not_3_out, and_6_out);
  and and_10 (and_10_out, not_3_out, and_7_out);
  nor nor_1 (nor_1_out, and_6_out, and_7_out);
  not not_4 (not_4_out, and_8_out);
  nor nor_2 (nor_2_out, and_8_out, and_9_out);
  assign FORWARD_A = and_6_out ? 2'b11 : 2'bz;  // Controlled_Buffer controlled_buffer_1
  assign FORWARD_A = and_10_out ? 2'b10 : 2'bz;  // Controlled_Buffer controlled_buffer_2
  assign FORWARD_A = nor_1_out ? 2'b00 : 2'bz;  // Controlled_Buffer controlled_buffer_3
  and and_11 (and_11_out, not_4_out, and_9_out);
  assign FORWARD_B = and_8_out ? 2'b11 : 2'bz;  // Controlled_Buffer controlled_buffer_4
  assign FORWARD_B = and_11_out ? 2'b10 : 2'bz;  // Controlled_Buffer controlled_buffer_5
  assign FORWARD_B = nor_2_out ? 2'b00 : 2'bz;  // Controlled_Buffer controlled_buffer_6
  D_Flip_Flop d_ff_1 (.clk(CLK), .D(and_5_out), .Q(d_ff_1_q));  // open: Qn, preset, reset
  not not_5 (not_5_out, and_5_out);
  // AND_Gate and_12 has open pins: in0=not_5_out, in1=and_5_out, out=open
  and and_13 (and_13_out, and_5_out, CLK);
  Counter #(.max('h2), .width(2)) counter_1 (
    .carry(counter_1_carry), .clk(and_13_out), .clr(and_15_out));  // open: load, D, count, Q, up
  and and_14 (and_14_out, d_ff_1_q, CLK);
  Counter #(.max('h2), .width(2)) counter_2 (
    .carry(counter_2_carry), .clk(and_14_out), .clr(and_16_out));  // open: load, D, count, Q, up
  not not_6 (not_6_out, d_ff_1_q);
  and and_15 (and_15_out, and_5_out, counter_1_carry);
  and and_16 (and_16_out, counter_2_carry, not_6_out);
  not not_7 (not_7_out, counter_2_carry);
  and and_17 (and_17_out, not_7_out, d_ff_1_q);
  or or_6 (STALL_DECODE, and_5_out, and_17_out);
  or or_7 (or_7_out, and_15_out, and_16_out);
  D_Flip_Flop d_ff_2 (.clk(CLK), .D(PC_SELECT), .Q(d_ff_2_q), .reset(counter_3_carry));  // open: Qn, preset
  and and_18 (and_18_out, CLK, d_ff_2_q);
  or or_8 (FLUSH_EXE, or_7_out, FLUSH_MEM);
  Counter #(.max('h1), .width(2)) counter_3 (
    .carry(counter_3_carry), .clk(and_18_out), .clr(counter_3_carry));  // open: load, D, count, Q, up
  or or_9 (FLUSH_DECODE, d_ff_2_q, PC_SELECT);
  and and_19 (FLUSH_MEM, counter_3_carry, d_ff_2_q);

  assign STALL_FETCH = STALL_DECODE;
endmodule
